# Fritzing sketch pi-serial-port-swarm (saved by Fritzing 0.9.9b)

parts:
  Raspberry_Pi_1 = Raspberry Pi 3 [part_number=RPI-3-V1.2]
  Componente3 = Adafruit 8x16 LED Matrix FeatherWing - White [part_number="Adafruit #3149"]

nets:
  GND: Raspberry_Pi_1.GND, Componente3.GND
  N1: Raspberry_Pi_1.GPIO15, Componente3.RX
  N2: Raspberry_Pi_1.GPIO14, Componente3.TX

custom parts:
  Adafruit 8x16 LED Matrix FeatherWing - White: You will chirp with delight when you see how easy it is to make your very own 8x16 LED matrix display for any Feather. This kit combines two of our adorable miniature LED matrices with a FeatherWing driver board. At 0.8" square, these little 8x8 matrices have got everything a big LED matrix has, but bite sized! Double them up for 128 total bright red LEDs. This is the White Adafruit 0.8" 8x16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
